# Fritzing sketch schema (saved by Fritzing 0.9.3b)
breadboards: 1

parts:
  Raspberry_Pi2 = Raspberry Pi 2
  Part2 = Arduino Uno (Rev3)
  LED2 = smd LED [color="Yellow (595nm)" package="0805 [SMD]"]  # not connected
  LED3 = smd LED [color="Green (555nm)" package="0805 [SMD]"]
  LED1 = smd LED [color="Red (633nm)" package="0603 [SMD]"]
  R1 = Resistor [tolerance=±5% resistance=220 package=THT]
  R2 = Resistor [tolerance=±5% resistance=220 package=THT]
  R3 = Resistor [tolerance=±5% resistance=220 package=THT]
  J1 = Infrared Proximity Sensor

nets:
  N1: Raspberry_Pi2.GPIO18, R3.Pin_0
  N2: Raspberry_Pi2.GPIO15, R2.Pin_0
  N3: Raspberry_Pi2.GPIO14, R1.Pin_0
  N4: Raspberry_Pi2.GND, LED1.cathode
  N5: Part2.A0, J1.Vout
  5V: Part2.5V, J1.Vcc
  GND: Part2.GND, J1.GND
  N6: LED3.anode, R3.Pin_1
  N7: LED1.anode, R1.Pin_1
