# Fritzing sketch schema (saved by Fritzing 0.9.3b)
breadboards: 1

parts:
  Part1 = Arduino Uno (Rev3)
  S1 = Momentary Switch [package=ksa_sealed_tac_switch]
  R1 = Resistor [tolerance=±5% resistance=330 package="0402 [SMD]"]
  S2 = Momentary Switch [package=ksa_sealed_tac_switch]
  S3 = Momentary Switch [package=ksa_sealed_tac_switch]
  R2 = Resistor [tolerance=±5% resistance=330 package="0402 [SMD]"]
  R3 = Resistor [tolerance=±5% resistance=330 package="0402 [SMD]"]

nets:
  N1: Part1.D2, S1.1
  N2: Part1.D3_PWM, S2.1
  N3: Part1.D4, S3.1
  N4: Part1.3V3, S1.4, S2.4, S3.4
  N5: Part1.GND, R1.Pin_0, R2.Pin_0, R3.Pin_0
  N6: S1.2, R1.Pin_1
  N7: S2.2, R2.Pin_1
  N8: S3.2, R3.Pin_1
